# Fritzing sketch Sinalizador de código Morse S.O.S. (saved by Fritzing 0.9.2b)
circuit board: 8.46667cm x 5.64444cm
breadboards: 1

parts:
  Componente1 = Arduino Uno (Rev3)
  LED1 = LED - 5mm [color="Red (633nm)" package="5 mm [THT]"]
  R1 = Resistor [tolerance=±5% resistance=330 package=THT]

nets:
  N1: Componente1.D10_PWM/SS, R1.Pin_1
  N2: Componente1.GND, LED1.cathode
  N3: LED1.anode, R1.Pin_0

// code stored in the sketch: Sinalizador_de_c_digo_Morse_S.O.S..ino
/* O padrão S.O.S. é formado de três pontos (sinais curtos), seguidos por três traços (sinais longos), seguidos por três pontos novamente. */

byte ledPin = 10;

void setup() {
  pinMode(ledPin, OUTPUT);
}

void loop() {
  //3 pontos
  for (byte x = 0; x < 3; x++) {
    digitalWrite(ledPin, HIGH);
    delay(150);
    digitalWrite(ledPin, LOW);
    delay(100);
  }

  //3 traços
  for (byte x = 0; x < 3; x++) {
    digitalWrite(ledPin, HIGH);
    delay(400);
    digitalWrite(ledPin, LOW);
    delay(100);
  }

  //3 pontos
  for (byte x = 0; x < 3; x++) {
    digitalWrite(ledPin, HIGH);
    delay(150);
    digitalWrite(ledPin, LOW);
    delay(100);
  }

  // Após 5 segundos, repete o sinal S.O.S.
  delay(5000);
}
