# Fritzing sketch Semáforo (saved by Fritzing 0.9.2b)
circuit board: 8.46667cm x 5.64444cm
breadboards: 1

parts:
  Componente1 = Arduino Uno (Rev3)
  R1 = Resistor [tolerance=±5% resistance=220 package=THT]
  Amarelo = LED - 5mm [color="Yellow (592nm)" package="5 mm [THT]"]
  Verde = LED - 5mm [color="Green (555nm)" package="5 mm [THT]"]
  R2 = Resistor [tolerance=±5% resistance=220 package=THT]
  R3 = Resistor [tolerance=±5% resistance=220 package=THT]
  Vermelho = LED - 5mm [color="Red (633nm)" package="5 mm [THT]"]

nets:
  N1: Componente1.D8, Verde.anode
  N2: Componente1.D9_PWM, Amarelo.anode
  N3: Componente1.D10_PWM/SS, Vermelho.anode
  N4: Componente1.GND, R1.Pin_0, R2.Pin_0, R3.Pin_0
  N5: R1.Pin_1, Vermelho.cathode
  N6: Amarelo.cathode, R2.Pin_1
  N7: Verde.cathode, R3.Pin_1

// code stored in the sketch: Semaforo.ino
int ledDelay = 10000;
byte redPin = 10;
byte yellowPin = 9;
byte greenPin = 8;

void setup() {
  pinMode(redPin, OUTPUT);
  pinMode(yellowPin, OUTPUT);
  pinMode(greenPin, OUTPUT);
}

void loop() {
  digitalWrite(redPin, HIGH);
  delay(ledDelay);

  digitalWrite(yellowPin, HIGH);
  delay(2000);

  digitalWrite(greenPin, HIGH);
  digitalWrite(redPin, LOW);
  digitalWrite(yellowPin, LOW);
  delay(ledDelay);

  digitalWrite(yellowPin, HIGH);
  digitalWrite(greenPin, LOW);
  delay(2000);

  digitalWrite(yellowPin, LOW);
}
